# Fritzing sketch OpenBot (saved by Fritzing 0.9.3b)

parts:
  Part1 = Arduino Uno (Rev3)
  M2 = DC Motor
  S1 = H-Bridge with L298N
  M3 = DC Motor
  S2 = Pololu QTR-8 Reflectabce Sensor array [package=THT]
  VCC2 = 4 x AAA Battery Mount
  U1 = SWITCH_SPDT [package=kps-1290]
  VCC1 = 4 x AAA Battery Mount

nets:
  N1: Part1.A0, S2.pin4, S2.pin6
  N2: Part1.A1, S2.pin7
  N3: Part1.A2, S2.pin8
  N4: Part1.A3, S2.pin9
  N5: Part1.A4/SDA, S2.pin10
  N6: Part1.A5/SCL, S2.pin11
  GND: Part1.GND, S1.GND, S2.pin1, S2.pin15, U1.S
  N7: Part1.D2, S1.ENB
  N8: Part1.D3_PWM, S1.IN4
  N9: Part1.D4, S1.IN3
  N10: Part1.D5_PWM, S1.IN2
  N11: Part1.D6_PWM, S1.IN1
  N12: Part1.D7, S1.ENA
  N13: Part1.5V, S2.pin2
  N14: Part1.VIN, VCC2.+
  N15: M2.pin_1, S1.M1-02
  N16: M2.pin_2, S1.M1-01
  N17: S1.12V, VCC1.+
  N18: S1.M2-01, M3.pin_2
  N19: S1.M2-02, M3.pin_1
  N20: VCC2.-, U1.P

notes:
  I think we can use only 1 switch like that one(I also couldnt find one like stm202)

custom parts:
  H-Bridge with L298N: h-bridge
