# Fritzing sketch OpenMOBot (saved by Fritzing 0.9.3b)

parts:
  M2 = DC Motor
  S1 = H-Bridge with L298N
  M3 = DC Motor
  S2 = Pololu QTR-8 Reflectabce Sensor array [package=THT]
  Part2 = FC-03 [chip_label=FC-03]
  Part3 = FC-03 [chip_label=FC-03]
  Part1 = Arduino Uno (Rev3)
  hc-sr1 = hc-sr04
  J1 = Basic Servo
  VCC4 = 4 x AAA Battery Mount
  S3 = SWITCH-DPDT [package=gpi-152-3013]
  VCC5 = 4 x AAA Battery Mount

nets:
  N1: M2.pin_1, S1.M2-02
  N2: M2.pin_2, S1.M2-01
  N3: S1.12V, S3.5
  GND: S1.GND, S2.pin1, S2.pin15, Part2.pin_2, Part3.pin_2, Part1.GND, hc-sr1.GND, J1.gnd, VCC4.-, VCC5.-
  N4: S1.ENA, Part1.D9_PWM
  N5: S1.IN1, Part1.D5_PWM
  N6: S1.IN2, Part1.D4
  N7: S1.IN3, Part1.D7
  N8: S1.IN4, Part1.D6_PWM
  N9: S1.ENB, Part1.D10_PWM/SS
  N10: S1.M1-01, M3.pin_2
  N11: S1.M1-02, M3.pin_1
  VCC: S2.pin2, S2.pin14, Part2.pin_1, Part3.pin_1, Part1.5V, hc-sr1.VCC, J1.vcc
  N12: S2.pin4, S2.pin6, Part1.A0
  N13: S2.pin7, Part1.A1
  N14: S2.pin8, Part1.A2
  N15: S2.pin9, Part1.A3
  N16: S2.pin10, Part1.A4/SDA
  N17: S2.pin11, Part1.A5/SCL
  N18: Part2.pin_3, Part1.D3_PWM
  N19: Part3.pin_3, Part1.D2
  N20: Part1.D8, hc-sr1.Trig
  N21: Part1.D11_PWM/MOSI, J1.pulse
  N22: Part1.D12/MISO, hc-sr1.Echo
  N23: Part1.VIN, S3.2
  N24: VCC4.+, S3.3
  N25: S3.6, VCC5.+

notes:
  Right Motor
  Left Motor
  Right Optocoupler
  Left Optocoupler
  Motor Driver
  HCSR-04
  QTR-8
  9 gram Servo
  Power Switch
  Motors Bateries
  Electronics Bateries

custom parts:
  H-Bridge with L298N: h-bridge
  FC-03: FC-03, LM393 IR Speed Sensor Encoder
